# Fritzing sketch openPFGE H1.0 (saved by Fritzing 0.9.3b)
circuit board: 5cm x 5cm
breadboards: 1

parts:
  HC05 = Bluetooth HC-05 Macho
  Servo = Header 3 [package=molex-1x3_lock]
  LCD = Header 4 [package=molex-1x4_lock]
  7805 = Voltage Regulator [package=to220-igo]
  Thermo = Header 2 [package=molex-1x2_lock]
  10K = Resistor [tolerance=±5% resistance=220 package=THT]
  On/Off = Toggle Switch [package=THT]
  Jack = Power Jack [package=power_jack_pth]
  Arduino_Nano = Arduino Nano (Rev3.0)

nets:
  N1: HC05.TXD, Arduino_Nano.D10
  N2: HC05.RXD, Arduino_Nano.D11/MOSI
  VCC: HC05.VCC, Servo.2, LCD.2, 7805.OUT, Arduino_Nano.5V
  GND: HC05.GND, Servo.1, LCD.1, 7805.GND, Thermo.1, Jack.GND, Jack.GNDBREAK, Arduino_Nano.GND
  N3: Servo.3, Arduino_Nano.D9
  N4: LCD.3, Arduino_Nano.A4
  N5: LCD.4, Arduino_Nano.A5
  N6: 7805.IN, On/Off.L2
  N7: Thermo.2, 10K.Pin_1, Arduino_Nano.A0
  N8: 10K.Pin_0, Arduino_Nano.AREF, Arduino_Nano.3V3
  N9: On/Off.COM, Jack.PWR

notes:
  H1.0
  openPFGE
  +
