# Fritzing sketch openPFGE H1.1 (saved by Fritzing 0.9.3b)
circuit board: 10cm x 5cm
breadboards: 1

parts:
  HC05 = Bluetooth HC-05 Macho
  LCD = Header 4 [package=molex-1x4_lock]
  7805 = Voltage Regulator [package=to220-igo]
  10K = Resistor [tolerance=±5% resistance=220 package=THT]
  Arduino_Nano = Arduino Nano (Rev3.0)
  Thermo = Screw terminal - 2 pins [package=THT]
  12V = Screw terminal - 2 pins [package=THT]
  Switch = Screw terminal - 2 pins [package=THT]
  Servo = screw terminal, 3 pins
  Fan_1 = Screw terminal - 2 pins [package=THT]
  Mosfet = Basic FET N-Channel [package="TO220 [THT]"]
  Mosfet_2 = Basic FET N-Channel [package="TO220 [THT]"]
  10K_2 = Resistor [tolerance=±5% resistance=220 package=THT]
  10K_3 = Resistor [tolerance=±5% resistance=220 package=THT]
  Pelt1 = Screw terminal - 2 pins [package=THT]
  Pelt2 = Screw terminal - 2 pins [package=THT]
  Mosfet_3 = Basic FET N-Channel [package="TO220 [THT]"]
  Mosfet_4 = Basic FET N-Channel [package="TO220 [THT]"]
  10K_4 = Resistor [tolerance=±5% resistance=220 package=THT]
  10K_5 = Resistor [tolerance=±5% resistance=220 package=THT]
  Diode = Rectifier Diode [part_number=1N4001 package="300 mil [THT]"]
  Diode_2 = Rectifier Diode [part_number=1N4001 package="300 mil [THT]"]
  Fan_2 = Screw terminal - 2 pins [package=THT]

nets:
  N1: HC05.TXD, Arduino_Nano.D10
  N2: HC05.RXD, Arduino_Nano.D11/MOSI
  VCC: HC05.VCC, LCD.2, 7805.OUT, Arduino_Nano.5V, Servo.pin2
  GND: HC05.GND, LCD.1, 7805.GND, Arduino_Nano.GND, Thermo.pin1, 12V.pin1, Servo.pin1, Mosfet.source, Mosfet_2.source, 10K_2.Pin_1, 10K_3.Pin_1, Mosfet_3.source, Mosfet_4.source, 10K_4.Pin_1, 10K_5.Pin_1
  N3: LCD.3, Arduino_Nano.A4
  N4: LCD.4, Arduino_Nano.A5
  N5: 7805.IN, Switch.pin2, Fan_1.pin2, Pelt1.pin2, Pelt2.pin2, Diode.cathode, Diode_2.cathode, Fan_2.pin2
  N6: 10K.Pin_0, Arduino_Nano.AREF, Arduino_Nano.3V3
  N7: 10K.Pin_1, Arduino_Nano.A0, Thermo.pin2
  N8: Arduino_Nano.D5, Mosfet_2.gate, 10K_2.Pin_0
  N9: Arduino_Nano.D6, Mosfet.gate, 10K_3.Pin_0
  N10: Arduino_Nano.D7, Mosfet_4.gate, 10K_5.Pin_0
  N11: Arduino_Nano.D8, Mosfet_3.gate, 10K_4.Pin_0
  N12: Arduino_Nano.D9, Servo.pin3
  N13: 12V.pin2, Switch.pin1
  N14: Fan_1.pin1, Mosfet_2.drain, Diode.anode
  N15: Mosfet.drain, Diode_2.anode, Fan_2.pin1
  N16: Pelt1.pin1, Mosfet_3.drain
  N17: Pelt2.pin1, Mosfet_4.drain

notes:
  +
  H1.1
  -
  +12V
  In
  +5V
  D9
  A0
  3.3V
  RX-D11
  SDA-A4
  SCL-A5
  TX-D10
  C  D  S
  Via
