# Fritzing sketch openPFGE H1.3 (saved by Fritzing 0.9.3b)
circuit board: 10cm x 5.05cm
breadboards: 1

parts:
  HC05 = Bluetooth HC-05 Macho
  LCD/OLED = Header 4 [package=molex-1x4_lock]
  7805 = Voltage Regulator [package=to220-igo]
  10K = Resistor [tolerance=±5% resistance=10k package=THT]
  Arduino_Nano = Arduino Nano (Rev3.0)
  Switch = Screw terminal - 2 pins [package=THT]
  Mosfet_F2 = Basic FET N-Channel [package="TO220 [THT]"]
  Mosfet_F1 = Basic FET N-Channel [package="TO220 [THT]"]
  10K_2 = Resistor [tolerance=±5% resistance=10k package=THT]
  10K_3 = Resistor [tolerance=±5% resistance=10k package=THT]
  Mosfet_P1 = Basic FET N-Channel [package="TO220 [THT]"]
  Mosfet_P2 = Basic FET N-Channel [package="TO220 [THT]"]
  10K_4 = Resistor [tolerance=±5% resistance=10k package=THT]
  10K_5 = Resistor [tolerance=±5% resistance=10k package=THT]
  Diode = Rectifier Diode [part_number=1N4001 package="300 mil [THT]"]
  Mosfet_P = Basic FET N-Channel [package="TO220 [THT]"]
  Diode_2 = Rectifier Diode [part_number=1N4001 package="300 mil [THT]"]
  10K_6 = Resistor [tolerance=±5% resistance=10k package=THT]
  10uF = Electrolytic Capacitor [capacitance=10µF package="100 mil [THT, electrolytic]"]
  100uF = Electrolytic Capacitor [capacitance=100µF package="100 mil [THT, electrolytic]"]
  Diode_3 = Rectifier Diode [part_number=1N4001 package="300 mil [THT]"]
  Fan_1 = Screw terminal - 2 pins [package=THT]
  Fan_2 = Screw terminal - 2 pins [package=THT]
  Pump = Screw terminal - 2 pins [package=THT]
  12V = Screw terminal - 2 pins [package=THT]
  Pelt1 = Screw terminal - 2 pins [package=THT]
  Pelt2 = Screw terminal - 2 pins [package=THT]
  Servo = screw terminal, 3 pins
  Thermo = Screw terminal - 2 pins [package=THT]
  Diode_4 = Rectifier Diode [part_number=1N4001 package="300 mil [THT]"]
  5V = Screw terminal - 2 pins [package=THT]

nets:
  N1: HC05.TXD, Arduino_Nano.D10
  N2: HC05.RXD, Arduino_Nano.D11/MOSI
  N3: HC05.VCC, LCD/OLED.2, 7805.OUT, 10uF.+, Servo.pin2, Diode_4.anode, 5V.pin2
  GND: HC05.GND, LCD/OLED.1, 7805.GND, Arduino_Nano.GND, Mosfet_F2.source, Mosfet_F1.source, 10K_2.Pin_1, 10K_3.Pin_1, Mosfet_P1.source, Mosfet_P2.source, 10K_4.Pin_1, 10K_5.Pin_1, Mosfet_P.source, 10K_6.Pin_1, 10uF.-, 100uF.-, 12V.pin1, Servo.pin1, Thermo.pin1, 5V.pin1
  N4: LCD/OLED.3, Arduino_Nano.A4
  N5: LCD/OLED.4, Arduino_Nano.A5
  N6: 7805.IN, Arduino_Nano.VIN, Switch.pin1, Diode.cathode, Diode_2.cathode, 100uF.+, Diode_3.cathode, Fan_1.pin2, Fan_2.pin2, Pump.pin2, Pelt1.pin2, Pelt2.pin2, Diode_4.cathode
  N7: 10K.Pin_0, Arduino_Nano.AREF, Arduino_Nano.3V3
  N8: 10K.Pin_1, Arduino_Nano.A0, Thermo.pin2
  N9: Arduino_Nano.D3, Mosfet_P.gate, 10K_6.Pin_0
  N10: Arduino_Nano.D5, Mosfet_F1.gate, 10K_2.Pin_0
  N11: Arduino_Nano.D6, Mosfet_F2.gate, 10K_3.Pin_0
  N12: Arduino_Nano.D7, Mosfet_P1.gate, 10K_4.Pin_0
  N13: Arduino_Nano.D8, Mosfet_P2.gate, 10K_5.Pin_0
  N14: Arduino_Nano.D9, Servo.pin3
  N15: Switch.pin2, 12V.pin2
  N16: Mosfet_F2.drain, Diode_3.anode, Fan_2.pin1
  N17: Mosfet_F1.drain, Diode.anode, Fan_1.pin1
  N18: Mosfet_P1.drain, Pelt1.pin1
  N19: Mosfet_P2.drain, Pelt2.pin1
  N20: Mosfet_P.drain, Diode_2.anode, Pump.pin1

notes:
  +
  H1.3
  + - TX RX
  -   + SDA SCL
  + -
  -  +  S
  out  in
